# Fritzing sketch MIDI (saved by Fritzing 0.6.3b)
breadboards: 1

parts:
  R1 = Rotary Potentiometer (Large) [maximum_resistance=10kΩ package=THT]
  R2 = Rotary Potentiometer (Large) [maximum_resistance=10kΩ package=THT]
  R3 = Rotary Potentiometer (Large) [maximum_resistance=10kΩ package=THT]
  R4 = Rotary Potentiometer (Large) [maximum_resistance=10kΩ package=THT]
  R5 = Resistor [tolerance=±5% resistance=220 package=THT]
  Arduino1 = Arduino
  DIN1 = DIN-5 jack (MIDI) [package=THT]

nets:
  N1: R1.leg1, R2.leg1, R3.leg1, R4.leg1, Arduino1.GND, DIN1.2
  N2: R1.wiper, Arduino1.A0
  N3: R1.leg2, R2.leg2, R3.leg2, R4.leg2, R5.Pin_0, Arduino1.+5V
  N4: R2.wiper, Arduino1.A3
  N5: R3.wiper, Arduino1.A2
  N6: R4.wiper, Arduino1.A1
  N7: R5.Pin_1, DIN1.4
  N8: Arduino1.D1TX, DIN1.5
